// Logisim project ex2.circ as structural Verilog: 6 circuits, main circuit AND2
module AND2 (
  input  A,
  input  B,
  output RESULT
);

  and and_1 (RESULT, A, B);

  // Notes on the sheet:
  //   Sample Circuit
endmodule

module NAND2 (
  input  A,
  input  B,
  output RESULT
);

  wire not_1_out, not_2_out;

  not not_1 (not_1_out, A);
  not not_2 (not_2_out, B);
  or or_1 (RESULT, not_1_out, not_2_out);
endmodule

module NOR2 (
  input  A,
  input  B,
  output RESULT
);

  wire not_1_out, not_2_out;

  not not_1 (not_1_out, A);
  not not_2 (not_2_out, B);
  and and_1 (RESULT, not_1_out, not_2_out);
endmodule

module XOR2 (
  input  A,
  input  B,
  output RESULT
);

  wire AAndNotB_out, not_1_out, not_2_out, NotAAndB_out;

  not not_1 (not_1_out, A);
  and NotAAndB (NotAAndB_out, not_1_out, B);
  and AAndNotB (AAndNotB_out, A, not_2_out);
  not not_2 (not_2_out, B);
  or or_1 (RESULT, NotAAndB_out, AAndNotB_out);
endmodule

module MUX2 (
  input  A,
  input  B,
  input  SEL,
  output RESULT
);

  wire AandSEL_out, BandCnot_out, not_1_out;

  not not_1 (not_1_out, SEL);
  and AandSEL (AandSEL_out, not_1_out, A);
  and BandCnot (BandCnot_out, B, SEL);
  or or_1 (RESULT, AandSEL_out, BandCnot_out);
endmodule

module MUX4 (
  input  A,
  input  B,
  input  C,
  input  D,
  input  SEL0,
  input  SEL1,
  output RESULT
);

  wire AandSEL_out, and_1_out, and_2_out, and_3_out, and_4_out, BandCnot_out, not_1_out, not_2_out, or_1_out,
       or_2_out;

  not not_1 (not_1_out, SEL0);
  and AandSEL (AandSEL_out, A, not_1_out);
  and BandCnot (BandCnot_out, B, SEL0);
  and and_1 (and_1_out, C, not_1_out);
  and and_2 (and_2_out, D, SEL0);
  or or_1 (or_1_out, AandSEL_out, BandCnot_out);
  or or_2 (or_2_out, and_1_out, and_2_out);
  not not_2 (not_2_out, SEL1);
  and and_3 (and_3_out, or_1_out, not_2_out);
  and and_4 (and_4_out, or_2_out, SEL1);
  or or_3 (RESULT, and_3_out, and_4_out);
endmodule
