// Logisim project ex6.circ as structural Verilog: 5 circuits, main circuit RotRight
module RotRight (
  input  [15:0] INPUT0,
  input  [3:0] AMOUNT,
  output [15:0] OUTPUT0
);

  wire [15:0] multiplexer_1_out, multiplexer_2_out, multiplexer_3_out;

  Multiplexer #(.enable("false"), .width(16)) multiplexer_1 (
    .in0(INPUT0), .in1({INPUT0[0], INPUT0[15:1]}), .out(multiplexer_1_out), .sel(AMOUNT[0]));
  Multiplexer #(.enable("false"), .width(16)) multiplexer_2 (
    .in0(multiplexer_1_out), .in1({multiplexer_1_out[1:0], multiplexer_1_out[15:2]}),
    .out(multiplexer_2_out), .sel(AMOUNT[1]));
  Multiplexer #(.enable("false"), .width(16)) multiplexer_3 (
    .in0(multiplexer_2_out), .in1({multiplexer_2_out[3:0], multiplexer_2_out[15:4]}),
    .out(multiplexer_3_out), .sel(AMOUNT[2]));
  Multiplexer #(.enable("false"), .width(16)) multiplexer_4 (
    .in0(multiplexer_3_out), .in1({multiplexer_3_out[7:0], multiplexer_3_out[15:8]}), .out(OUTPUT0),
    .sel(AMOUNT[3]));
endmodule

module rot1 (
  input  [15:0] in_1,
  output [15:0] out_2
);
endmodule

module rot2 (
  input  [15:0] in_1,
  output [15:0] out_2
);
endmodule

module rot4 (
  input  [15:0] in_1,
  output [15:0] out_2
);
endmodule

module rot8 (
  input  [15:0] in_1,
  output [15:0] out_2
);
endmodule
