// Logisim project alu.circ as structural Verilog
module alu (
  input  [31:0] A,
  input  [31:0] B,
  input  [3:0] ALUSel,
  output [31:0] Result
);

  wire [0:0] SLT_T;
  wire [31:0] AB_AND, AB_OR, AB_XOR, add0, MUL_AB, MULH_AB, MULHU_AB, SL_L, SR_L, SRA_AB, SUB_AB;

  Multiplier #(.mode("twosComplement"), .width(32)) multiplier_1 (
    .a(A), .b(B), .out(MUL_AB), .cout(MULH_AB));  // open: cin
  Multiplier #(.width(32)) multiplier_2 (.a(A), .b(B), .cout(MULHU_AB));  // open: out, cin
  Adder #(.width(32)) adder_1 (.a(A), .b(B), .out(add0));  // open: cin, cout
  Shifter #(.width(32)) shifter_1 (.in(A), .\dist (B[4:0]), .out(SL_L));
  Comparator #(.width(32)) comparator_1 (.a(A), .b(B), .lt(SLT_T[0]));  // open: gt, eq
  assign AB_XOR = A ^ B;  // XOR_Gate xor_1, 32 bits wide
  Shifter #(.shift("lr"), .width(32)) shifter_2 (.in(A), .\dist (B[4:0]), .out(SR_L));
  assign AB_OR = A | B;  // OR_Gate or_1, 32 bits wide
  assign AB_AND = A & B;  // AND_Gate and_1, 32 bits wide
  Subtractor #(.width(32)) subtractor_1 (.a(A), .b(B), .out(SUB_AB));  // open: bin, bout
  Shifter #(.shift("ar"), .width(32)) shifter_3 (.in(A), .\dist (B[4:0]), .out(SRA_AB));
  Multiplexer #(.enable("false"), .select(4), .width(32)) multiplexer_1 (
    .in0(add0), .in1(SL_L), .in2({{31{1'b0}}, SLT_T[0]}), .in4(AB_XOR), .in5(SR_L), .in6(AB_OR),
    .in7(AB_AND), .in8(MUL_AB), .in9(MULH_AB), .in11(MULHU_AB), .in12(SUB_AB), .in13(SRA_AB), .in15(B),
    .out(Result), .sel(ALUSel));  // open: in3, in10, in14

  // Other names for the same wires on the sheet: B_shift[4:0] = B[4:0]

  // Notes on the sheet:
  //   INPUTS to your circuit
  //   ALU OPERATORS
  //   DON'T CHANGE THE LOCATIONS OF THE INPUTS AND OUTPUTS!
  //   ALU MUX
  //   OUTPUT from your circuit
endmodule
