// Logisim project branch-comp.circ as structural Verilog: 1 circuit, main circuit branch_comp
module branch_comp (
  input  [31:0] rs1,
  input  [31:0] rs2,
  input  BrUn,
  output BrEq,
  output BrLt
);

  wire comparator_1_gt, comparator_2_eq, comparator_3_eq, comparator_4_gt;

  Comparator #(.width(32)) comparator_1 (.a(rs2), .b(rs1), .gt(comparator_1_gt));  // open: eq, lt
  Comparator #(.width(32)) comparator_2 (.a(rs2), .b(rs1), .eq(comparator_2_eq));  // open: gt, lt
  Comparator #(.mode("unsigned"), .width(32)) comparator_3 (.a(rs2), .b(rs1), .eq(comparator_3_eq));  // open: gt, lt
  Comparator #(.mode("unsigned"), .width(32)) comparator_4 (.a(rs2), .b(rs1), .gt(comparator_4_gt));  // open: eq, lt
  Multiplexer #(.enable("false")) multiplexer_1 (.in0(comparator_2_eq), .in1(comparator_3_eq), .out(BrEq), .sel(BrUn));
  Multiplexer #(.enable("false")) multiplexer_2 (.in0(comparator_1_gt), .in1(comparator_4_gt), .out(BrLt), .sel(BrUn));

  // Notes on the sheet:
  //   INPUTS to your circuit
  //   DON'T CHANGE THE LOCATIONS OF THE INPUTS AND OUTPUTS!
  //   OUTPUT from your circuit
endmodule
