// Logisim project control-logic.circ as structural Verilog: 1 circuit, main circuit control_logic
module control_logic (
  input  [31:0] inst,
  input  BrEq,
  input  BrLt,
  output PCSel,
  output RegWEn,
  output [2:0] ImmSel,
  output BrUn,
  output ASel,
  output BSel,
  output [3:0] ALUSel,
  output MemRW,
  output [1:0] WBSel,
  output CSRSel,
  output CSRWen
);

  wire add, addi, and_27_out, and_28_out, and_29_out, and_30_out, and_31_out, and_32_out, and_R, andi, beq,
       bge, bgeu, blt, bltu, bne, f3_is_0, f3_is_1, f3_is_2, f3_is_3, f3_is_4, f3_is_5, f3_is_6, f3_is_7,
       f7_is_0, f7_is_01, f7_is_20, is_CSR, is_I, is_jalr_I, is_load_I, is_lui, is_R, is_S, is_SB, is_U,
       is_UJ, mul, mulh, mulhu, not_1_out, not_2_out, or_1_out, or_2_out, or_3_out, or_4_out, or_R, ori,
       sll_R, slli, slt, slti, sra_R, srai, srl_R, srli, sub, xor_1_out, xor_2_out, xor_R, xori;
  wire [4:0] ROM_OUT;

  and and_1 (sll_R, is_R, f7_is_0, f3_is_1);
  and and_2 (mulh, f3_is_1, f7_is_01, is_R);
  and and_3 (mulhu, f3_is_3, is_R, f7_is_01);
  and and_4 (srl_R, is_R, f7_is_0, f3_is_5);
  and and_5 (sra_R, f3_is_5, f7_is_20, is_R);
  and and_6 (and_R, f3_is_7, f7_is_0);
  and and_7 (bge, f3_is_5, is_SB);
  and and_8 (bltu, f3_is_6, is_SB);
  and and_9 (bgeu, f3_is_7, is_SB);
  Comparator #(.mode("unsigned"), .width(7)) comparator_1 (.a(inst[6:0]), .b(7'b0110011), .eq(is_R));  // open: gt, lt
  Comparator #(.mode("unsigned"), .width(7)) comparator_2 (
    .a(inst[6:0]), .b(7'b0000011), .eq(is_load_I));  // open: gt, lt
  Comparator #(.mode("unsigned"), .width(7)) comparator_3 (.a(inst[6:0]), .b(7'b0010011), .eq(is_I));  // open: gt, lt
  Comparator #(.mode("unsigned"), .width(7)) comparator_4 (.a(inst[6:0]), .b(7'b0100011), .eq(is_S));  // open: gt, lt
  Comparator #(.mode("unsigned"), .width(7)) comparator_5 (.a(inst[6:0]), .b(7'b1100011), .eq(is_SB));  // open: gt, lt
  ROM #(.addrWidth(6), .dataWidth(16)) rom_1 (
    .addr({1'b0, ROM_OUT}), .data({RegWEn, ImmSel, BrUn, ASel, BSel, ALUSel, MemRW, WBSel, CSRSel, CSRWen}));
  and and_10 (addi, is_I, f3_is_0);
  and and_11 (slli, is_I, f7_is_0, f3_is_1);
  and and_12 (slti, is_I, f3_is_2);
  and and_13 (xori, is_I, f3_is_4);
  and and_14 (srli, is_I, f7_is_0, f3_is_5);
  and and_15 (srai, f3_is_5, is_I, f7_is_20);
  and and_16 (ori, is_I, f3_is_6);
  and and_17 (andi, is_I, f3_is_7);
  and and_18 (add, is_R, f3_is_0, f7_is_0);
  and and_19 (mul, is_R, f3_is_0, f7_is_01);
  and and_20 (sub, is_R, f3_is_0, f7_is_20);
  and and_21 (slt, f3_is_2, is_R, f7_is_0);
  and and_22 (xor_R, f3_is_4, is_R, f7_is_0);
  and and_23 (or_R, f3_is_6, is_R, f7_is_0);
  and and_24 (beq, f3_is_0, is_SB);
  and and_25 (bne, f3_is_1, is_SB);
  and and_26 (blt, f3_is_4, is_SB);
  Comparator #(.mode("unsigned"), .width(7)) comparator_6 (.a(inst[6:0]), .b(7'b0010111), .eq(is_U));  // open: gt, lt
  Comparator #(.mode("unsigned"), .width(7)) comparator_7 (.a(inst[6:0]), .b(7'b1101111), .eq(is_UJ));  // open: gt, lt
  Comparator #(.mode("unsigned"), .width(7)) comparator_8 (
    .a(inst[6:0]), .b(7'b1100111), .eq(is_jalr_I));  // open: gt, lt
  Comparator #(.mode("unsigned"), .width(7)) comparator_9 (.a(inst[6:0]), .b(7'b1110011), .eq(is_CSR));  // open: gt, lt
  Comparator #(.mode("unsigned"), .width(7)) comparator_10 (
    .a(inst[6:0]), .b(7'b0110111), .eq(is_lui));  // open: gt, lt
  Comparator #(.mode("unsigned"), .width(3)) comparator_11 (.a(inst[14:12]), .b(3'b000), .eq(f3_is_0));  // open: gt, lt
  Comparator #(.mode("unsigned"), .width(3)) comparator_12 (.a(inst[14:12]), .b(3'b001), .eq(f3_is_1));  // open: gt, lt
  Comparator #(.mode("unsigned"), .width(3)) comparator_13 (.a(inst[14:12]), .b(3'b010), .eq(f3_is_2));  // open: gt, lt
  Comparator #(.mode("unsigned"), .width(3)) comparator_14 (.a(inst[14:12]), .b(3'b100), .eq(f3_is_4));  // open: gt, lt
  Comparator #(.mode("unsigned"), .width(7)) comparator_15 (
    .a(inst[31:25]), .b({7{1'b0}}), .eq(f7_is_0));  // open: gt, lt
  Comparator #(.mode("unsigned"), .width(7)) comparator_16 (
    .a(inst[31:25]), .b(7'b0100000), .eq(f7_is_20));  // open: gt, lt
  Comparator #(.mode("unsigned"), .width(7)) comparator_17 (
    .a(inst[31:25]), .b(7'b0000001), .eq(f7_is_01));  // open: gt, lt
  Comparator #(.mode("unsigned"), .width(3)) comparator_18 (.a(inst[14:12]), .b(3'b101), .eq(f3_is_5));  // open: gt, lt
  Comparator #(.mode("unsigned"), .width(3)) comparator_19 (.a(inst[14:12]), .b(3'b011), .eq(f3_is_3));  // open: gt, lt
  Comparator #(.mode("unsigned"), .width(3)) comparator_20 (.a(inst[14:12]), .b(3'b110), .eq(f3_is_6));  // open: gt, lt
  Comparator #(.mode("unsigned"), .width(3)) comparator_21 (.a(inst[14:12]), .b(3'b111), .eq(f3_is_7));  // open: gt, lt
  and and_27 (and_27_out, is_jalr_I, f3_is_0);
  and and_28 (and_28_out, is_CSR, f3_is_1);
  and and_29 (and_29_out, is_CSR, f3_is_5);
  or or_1 (or_1_out, beq, bne, blt, bge);
  or or_2 (or_2_out, bltu, bgeu);
  Priority_Encoder #(.select(5)) priority_encoder_1 (
    .in0(add), .in1(mul), .in2(sub), .in3(sll_R), .in4(mulh), .in5(mulhu), .in6(slt), .in7(xor_R),
    .in8(srl_R), .in9(sra_R), .in10(or_R), .in11(and_R), .in12(is_load_I), .in15(addi), .in16(slli),
    .in17(slti), .in18(xori), .in19(srli), .in20(srai), .in21(ori), .in22(andi), .in23(is_S), .in24(is_U),
    .in25(is_lui), .in26(is_UJ), .in27(and_27_out), .in28(and_28_out), .in29(and_29_out), .in30(or_1_out),
    .in31(or_2_out), .out(ROM_OUT));  // open: in13, in14, gs, en_out, en_in
  xor xor_1 (xor_1_out, inst[12], BrEq);
  or or_3 (or_3_out, inst[13], inst[14]);
  xor xor_2 (xor_2_out, inst[12], BrLt);
  and and_30 (and_30_out, xor_1_out, not_1_out);
  not not_1 (not_1_out, or_3_out);
  and and_31 (and_31_out, inst[14], xor_2_out);
  not not_2 (not_2_out, inst[4]);
  or or_4 (or_4_out, and_30_out, and_31_out, inst[2]);
  and and_32 (and_32_out, inst[6], not_2_out);
  and and_33 (PCSel, or_4_out, and_32_out);

  // Other names for the same wires on the sheet: OPCODE[6:0] = inst[6:0]; OP_2 = inst[2]; OP_4 = inst[4];
  //   OP_6 = inst[6]; RD[4:0] = inst[11:7]; f_30 = inst[12]; FUNC3[2:0] = inst[14:12]; f_31 = inst[13];
  //   f_32 = inst[14]; RS1[4:0] = inst[19:15]; RS2[4:0] = inst[24:20]; f_70 = inst[25]; FUNC7[6:0] = inst[31:25];
  //   f_71 = inst[26]; f_72 = inst[27]; f_73 = inst[28]; f_74 = inst[29]; f_75 = inst[30]; f_76 = inst[31]

  // Notes on the sheet:
  //   INPUTS to your circuit
  //   Connect ROM Input here ->
  //   I Type Dictionary
  //   SB Type Dictionary
  //   R Type Dictionary
  //   contents of rom_1 (hex, n*v repeats v):
  //   8004 8104 8184 8024 8124 8164 8044 8084 80a4 81a4 80c4 80e4 8208 8208 8208 8204 8224 8244 8284 82a4
  //   83a4 82c4 82e4 1210 b604 b7e4 c600 8200 5001 5203 2600 2e00 c604 c204 d604 8204 4 3203
  //   ROM FOR CONTROL LOGIC
  //   DON'T CHANGE THE LOCATIONS OF THE INPUTS AND OUTPUTS!
  //   OUTPUT from your circuit
  //   Hard Coded Types
  //   CLOSE
  //   WIRE
  //   TO
  //   USE
  //   ROM
  //   Reminder: Use combinational logic for PCSel
  //   PCSel Logic
endmodule
