// Logisim project cpu.circ as structural Verilog: 1 circuit, main circuit cpu
module cpu (
  input  clk,
  input  [31:0] INSTRUCTION,
  input  [31:0] MEM_READ_DATA,
  output [31:0] MEM_WRITE_ADDRESS,
  output [31:0] PROGRAM_COUNTER,
  output [31:0] ra,
  output [31:0] sp,
  output [31:0] t0,
  output [31:0] t1,
  output [31:0] t2,
  output [31:0] s0,
  output [31:0] s1,
  output [31:0] a0,
  output [31:0] tohost,
  output [3:0] MEM_WRITE_ENABLE,
  output [31:0] MEM_WRITE_DATA
);

  wire ASel, BrEq, BrLt, BrUn, BSel, control_logic_1_csrsel, control_logic_1_csrwen, MemRW, PCSel, RegWEN;
  wire [1:0] B, WB_SEL;
  wire [2:0] ImmSel;
  wire [3:0] ALUSel, multiplexer_9_out, multiplexer_10_out, multiplexer_15_out;
  wire [7:0] multiplexer_7_out;
  wire [11:0] csr_add;
  wire [15:0] multiplexer_8_out, multiplexer_12_out;
  wire [19:0] Current_INSTRUCTION;
  wire [23:0] multiplexer_11_out;
  wire [31:0] adder_2_out, Current_PC, DATA, imm_gen_1_imm, Mem_Read, multiplexer_1_out, multiplexer_2_out,
       multiplexer_3_out, multiplexer_4_out, multiplexer_5_out, multiplexer_13_out, multiplexer_14_out, PC_4,
       regfile_1_read_data_1, wb;

  Multiplexer #(.enable("false"), .width(32)) multiplexer_1 (
    .in0(PC_4), .in1({MEM_WRITE_ADDRESS[31:2], B}), .out(multiplexer_1_out), .sel(PCSel));
  control_logic control_logic_1 (
    .CSRWen(control_logic_1_csrwen), .PCSel(PCSel), .RegWEn(RegWEN), .ImmSel(ImmSel), .BrUn(BrUn),
    .ASel(ASel), .BSel(BSel), .ALUSel(ALUSel), .MemRW(MemRW), .WBSel(WB_SEL),
    .CSRSel(control_logic_1_csrsel), .inst({csr_add, Current_INSTRUCTION}), .BrEq(BrEq), .BrLt(BrLt));
  Adder #(.width(32)) adder_1 (.a(PROGRAM_COUNTER), .b(32'h4), .out(PC_4));  // open: cin, cout
  Register #(.width(32)) PC (.D(multiplexer_1_out), .clk(clk), .Q(PROGRAM_COUNTER));  // open: en, clr
  imm_gen imm_gen_1 (.inst({csr_add, Current_INSTRUCTION}), .ImmSel(ImmSel), .imm(imm_gen_1_imm));
  Register #(.width(32)) register_1 (
    .D(multiplexer_2_out), .clk(clk), .Q({csr_add, Current_INSTRUCTION}));  // open: en, clr
  Multiplexer #(.enable("false"), .width(32)) multiplexer_2 (
    .in0(INSTRUCTION), .in1(32'h13), .out(multiplexer_2_out), .sel(PCSel));
  Register #(.width(32)) register_2 (.D(PROGRAM_COUNTER), .clk(clk), .Q(Current_PC));  // open: en, clr
  regfile regfile_1 (
    .rs1(Current_INSTRUCTION[19:15]), .rs2(csr_add[4:0]), .rd(Current_INSTRUCTION[11:7]), .Write_Data(wb),
    .RegWEn(RegWEN), .clk(clk), .ra(ra), .sp(sp), .t0(t0), .t1(t1), .t2(t2), .s0(s0), .s1(s1), .a0(a0),
    .Read_Data_1(regfile_1_read_data_1), .Read_Data_2(DATA));
  branch_comp branch_comp_1 (.rs1(regfile_1_read_data_1), .rs2(DATA), .BrUn(BrUn), .BrEq(BrEq), .BrLt(BrLt));
  Multiplexer #(.enable("false"), .width(32)) multiplexer_3 (
    .in0(regfile_1_read_data_1), .in1(imm_gen_1_imm), .out(multiplexer_3_out), .sel(control_logic_1_csrsel));
  Multiplexer #(.enable("false"), .width(32)) multiplexer_4 (
    .in0(regfile_1_read_data_1), .in1(Current_PC), .out(multiplexer_4_out), .sel(ASel));
  Multiplexer #(.enable("false"), .width(32)) multiplexer_5 (
    .in0(DATA), .in1(imm_gen_1_imm), .out(multiplexer_5_out), .sel(BSel));
  alu alu_1 (.Result({MEM_WRITE_ADDRESS[31:2], B}), .A(multiplexer_4_out), .B(multiplexer_5_out), .ALUSel(ALUSel));
  // csr csr_1: pin names not known; wires that end beside it: csr_add, multiplexer_3_out, control_logic_1_csrwen, clk, tohost
  Adder #(.width(32)) adder_2 (.a(Current_PC), .b(32'h4), .out(adder_2_out));  // open: cin, cout
  Multiplexer #(.enable("false"), .select(2), .width(32)) multiplexer_6 (
    .in0(adder_2_out), .in1({MEM_WRITE_ADDRESS[31:2], B}), .in2(Mem_Read), .out(wb), .sel(WB_SEL));  // open: in3
  Multiplexer #(.enable("false"), .select(2), .width(8)) multiplexer_7 (
    .in0(MEM_READ_DATA[7:0]), .in1(MEM_READ_DATA[15:8]), .in2(MEM_READ_DATA[23:16]),
    .in3(MEM_READ_DATA[31:24]), .out(multiplexer_7_out), .sel(B));
  Multiplexer #(.enable("false"), .width(16)) multiplexer_8 (
    .in0(MEM_READ_DATA[15:0]), .in1(MEM_READ_DATA[31:16]), .out(multiplexer_8_out), .sel(B[1]));
  Multiplexer #(.enable("false"), .select(2), .width(4)) multiplexer_9 (
    .in0(4'b0001), .in1(4'b0010), .in2(4'b0100), .in3(4'b1000), .out(multiplexer_9_out), .sel(B));
  Multiplexer #(.enable("false"), .width(4)) multiplexer_10 (
    .in0(4'b0011), .in1(4'b1100), .out(multiplexer_10_out), .sel(B[1]));
  Multiplexer #(.enable("false"), .width(24)) multiplexer_11 (
    .in0({24{1'b0}}), .in1({24{1'b1}}), .out(multiplexer_11_out), .sel(multiplexer_7_out[7]));
  Multiplexer #(.enable("false"), .width(16)) multiplexer_12 (
    .in0({16{1'b0}}), .in1({16{1'b1}}), .out(multiplexer_12_out), .sel(multiplexer_8_out[15]));
  Multiplexer #(.enable("false"), .select(2), .width(32)) multiplexer_13 (
    .in0({{24{1'b0}}, DATA[7:0]}), .in1({{16{1'b0}}, DATA[7:0], {8{1'b0}}}),
    .in2({{8{1'b0}}, DATA[7:0], {16{1'b0}}}), .in3({DATA[7:0], {24{1'b0}}}), .out(multiplexer_13_out), .sel(B));
  Multiplexer #(.enable("false"), .width(32)) multiplexer_14 (
    .in0({{16{1'b0}}, DATA[15:0]}), .in1({DATA[15:0], {16{1'b0}}}), .out(multiplexer_14_out), .sel(B[1]));
  Multiplexer #(.enable("false"), .select(2), .width(4)) multiplexer_15 (
    .in0(multiplexer_9_out), .in1(multiplexer_10_out), .in2(4'b1111), .out(multiplexer_15_out),
    .sel(Current_INSTRUCTION[13:12]));  // open: in3
  Multiplexer #(.enable("false"), .select(2), .width(32)) multiplexer_16 (
    .in0({multiplexer_11_out, multiplexer_7_out}), .in1({multiplexer_12_out, multiplexer_8_out}),
    .in2(MEM_READ_DATA), .out(Mem_Read), .sel(Current_INSTRUCTION[13:12]));  // open: in3
  Multiplexer #(.enable("false"), .width(4)) multiplexer_17 (
    .in0(4'b0000), .in1(multiplexer_15_out), .out(MEM_WRITE_ENABLE), .sel(MemRW));
  Multiplexer #(.enable("false"), .select(2), .width(32)) multiplexer_18 (
    .in0(multiplexer_13_out), .in1(multiplexer_14_out), .in2(DATA), .out(MEM_WRITE_DATA),
    .sel(Current_INSTRUCTION[13:12]));  // open: in3

  assign MEM_WRITE_ADDRESS[1:0] = 2'b00;

  // Other names for the same wires on the sheet: OPCODE[6:0] = Current_INSTRUCTION[6:0];
  //   RD[4:0] = Current_INSTRUCTION[11:7]; FUNC3[2:0] = Current_INSTRUCTION[14:12];
  //   RS1[4:0] = Current_INSTRUCTION[19:15]; Current_INSTRUCTION[31:20] = csr_add; RS2[4:0] = csr_add[4:0];
  //   FUNC7[6:0] = csr_add[11:5]; Result[31:0] = {MEM_WRITE_ADDRESS[31:2], B}

  // Notes on the sheet:
  //   Output to IMEM
  //   IMEM (do **NOT** move this)
  //   Inputs from IMEM
  //   SPLITER
  //   It is OK to move the PC, RegFile, ALU, MEM, Branch Comp, Imm Gen, and Control Logic to wherever is most convenient for you when constructing your CPU, and to delete this text
  //   Inputs/Outputs for testing. Do **NOT** move these.
  //   Outputs To DMEM
  //   DMEM (do **NOT** move this)
  //   Inputs From DMEM
endmodule
