// Logisim project cpu_first_design.circ as structural Verilog: 1 circuit, main circuit cpu
module cpu (
  input  clk,
  input  [31:0] INSTRUCTION,
  input  [31:0] MEM_READ_DATA,
  output [31:0] MEM_WRITE_ADDRESS,
  output [31:0] PROGRAM_COUNTER,
  output [31:0] ra,
  output [31:0] sp,
  output [31:0] t0,
  output [31:0] t1,
  output [31:0] t2,
  output [31:0] s0,
  output [31:0] s1,
  output [31:0] a0,
  output [31:0] tohost,
  output [3:0] MEM_WRITE_ENABLE,
  output [31:0] MEM_WRITE_DATA
);

  wire and_1_out, and_2_out, and_3_out, and_4_out, and_5_out, and_6_out, and_7_out, ASel, Bottom2_is_0,
       Bottom2_is_1, Bottom2_is_2, Bottom2_is_3, BrEq, BrLt, BrUn, BSel, f3_is_0, f3_is_1, f3_is_2, MemRW,
       PCSel, RegWEN;
  wire [1:0] WB_SEL;
  wire [2:0] ImmSel;
  wire [3:0] ALUSel, select_bits_for_reading;
  wire [16:0] multiplexer_9_out, multiplexer_10_out;
  wire [24:0] multiplexer_5_out, multiplexer_6_out, multiplexer_7_out, multiplexer_8_out;
  wire [31:0] Address, imm_gen_1_imm, MEM_Read, multiplexer_1_out, multiplexer_2_out, multiplexer_3_out,
       PC_4, regfile_1_read_data_1, wb;

  Adder #(.width(32)) adder_1 (.a(PROGRAM_COUNTER), .b(32'h4), .out(PC_4));  // open: cin, cout
  Register #(.width(32)) PC (.D(multiplexer_1_out), .clk(clk), .Q(PROGRAM_COUNTER));  // open: en, clr
  Multiplexer #(.enable("false"), .width(32)) multiplexer_1 (
    .in0(PC_4), .in1(Address), .out(multiplexer_1_out), .sel(PCSel));
  control_logic control_logic_1 (
    .PCSel(PCSel), .RegWEn(RegWEN), .ImmSel(ImmSel), .BrUn(BrUn), .ASel(ASel), .BSel(BSel), .ALUSel(ALUSel),
    .MemRW(MemRW), .WBSel(WB_SEL), .inst(INSTRUCTION), .BrEq(BrEq), .BrLt(BrLt));  // open: CSRWen, CSRSel
  imm_gen imm_gen_1 (.inst(INSTRUCTION), .ImmSel(ImmSel), .imm(imm_gen_1_imm));
  regfile regfile_1 (
    .rs1(INSTRUCTION[19:15]), .rs2(INSTRUCTION[24:20]), .rd(INSTRUCTION[11:7]), .Write_Data(wb),
    .RegWEn(RegWEN), .clk(clk), .ra(ra), .sp(sp), .t0(t0), .t1(t1), .t2(t2), .s0(s0), .s1(s1), .a0(a0),
    .Read_Data_1(regfile_1_read_data_1), .Read_Data_2(MEM_WRITE_DATA));
  branch_comp branch_comp_1 (.rs1(regfile_1_read_data_1), .rs2(MEM_WRITE_DATA), .BrUn(BrUn), .BrEq(BrEq), .BrLt(BrLt));
  Multiplexer #(.enable("false"), .width(32)) multiplexer_2 (
    .in0(regfile_1_read_data_1), .in1(PROGRAM_COUNTER), .out(multiplexer_2_out), .sel(ASel));
  Multiplexer #(.enable("false"), .width(32)) multiplexer_3 (
    .in0(MEM_WRITE_DATA), .in1(imm_gen_1_imm), .out(multiplexer_3_out), .sel(BSel));
  alu alu_1 (.Result(Address), .A(multiplexer_2_out), .B(multiplexer_3_out), .ALUSel(ALUSel));
  // csr csr_1: pin names not known; wires that end beside it: tohost
  Multiplexer #(.enable("false"), .select(2), .width(32)) multiplexer_4 (
    .in0(PC_4), .in1(Address), .in2(MEM_Read), .out(wb), .sel(WB_SEL));  // open: in3
  Comparator #(.mode("unsigned"), .width(3)) comparator_1 (
    .a(INSTRUCTION[14:12]), .b(3'b000), .eq(f3_is_0));  // open: gt, lt
  Comparator #(.mode("unsigned"), .width(3)) comparator_2 (
    .a(INSTRUCTION[14:12]), .b(3'b001), .eq(f3_is_1));  // open: gt, lt
  Comparator #(.mode("unsigned"), .width(3)) comparator_3 (
    .a(INSTRUCTION[14:12]), .b(3'b010), .eq(f3_is_2));  // open: gt, lt
  and and_1 (and_1_out, Bottom2_is_0, f3_is_0);
  and and_2 (and_2_out, Bottom2_is_1, f3_is_0);
  and and_3 (and_3_out, Bottom2_is_2, f3_is_0);
  and and_4 (and_4_out, Bottom2_is_3, f3_is_0);
  and and_5 (and_5_out, f3_is_1, Bottom2_is_0);
  and and_6 (and_6_out, f3_is_1, Bottom2_is_2);
  and and_7 (and_7_out, f3_is_2, Bottom2_is_0);
  Multiplexer #(.enable("false"), .width(25)) multiplexer_5 (
    .in0({25{1'b0}}), .in1({25{1'b1}}), .out(multiplexer_5_out), .sel(MEM_READ_DATA[7]));
  Multiplexer #(.enable("false"), .width(25)) multiplexer_6 (
    .in0({25{1'b0}}), .in1({25{1'b1}}), .out(multiplexer_6_out), .sel(MEM_READ_DATA[15]));
  Multiplexer #(.enable("false"), .width(25)) multiplexer_7 (
    .in0({25{1'b0}}), .in1({25{1'b1}}), .out(multiplexer_7_out), .sel(MEM_READ_DATA[23]));
  Multiplexer #(.enable("false"), .width(25)) multiplexer_8 (
    .in0({25{1'b0}}), .in1({25{1'b1}}), .out(multiplexer_8_out), .sel(MEM_READ_DATA[31]));
  Multiplexer #(.enable("false"), .width(17)) multiplexer_9 (
    .in0({17{1'b0}}), .in1({17{1'b1}}), .out(multiplexer_9_out), .sel(MEM_READ_DATA[15]));
  Multiplexer #(.enable("false"), .width(17)) multiplexer_10 (
    .in0({17{1'b0}}), .in1({17{1'b1}}), .out(multiplexer_10_out), .sel(MEM_READ_DATA[31]));
  Priority_Encoder #(.select(4)) priority_encoder_1 (
    .in1(and_1_out), .in2(and_2_out), .in3(and_5_out), .in4(and_3_out), .in8(and_4_out), .in12(and_6_out),
    .in15(and_7_out), .out(select_bits_for_reading));  // open: in0, in5, in6, in7, in9, in10, in11, in13, in14, gs, en_out, en_in
  Multiplexer #(.enable("false"), .width(4)) multiplexer_11 (
    .in0(4'b0000), .in1(select_bits_for_reading), .out(MEM_WRITE_ENABLE), .sel(MemRW));
  Comparator #(.mode("unsigned"), .width(2)) comparator_4 (
    .a(Address[1:0]), .b(2'b00), .eq(Bottom2_is_0));  // open: gt, lt
  Comparator #(.mode("unsigned"), .width(2)) comparator_5 (
    .a(Address[1:0]), .b(2'b01), .eq(Bottom2_is_1));  // open: gt, lt
  Comparator #(.mode("unsigned"), .width(2)) comparator_6 (
    .a(Address[1:0]), .b(2'b10), .eq(Bottom2_is_2));  // open: gt, lt
  Comparator #(.mode("unsigned"), .width(2)) comparator_7 (
    .a(Address[1:0]), .b(2'b11), .eq(Bottom2_is_3));  // open: gt, lt
  Multiplexer #(.enable("false"), .select(4), .width(32)) multiplexer_12 (
    .in1({multiplexer_5_out, MEM_READ_DATA[6:0]}), .in2({multiplexer_6_out, MEM_READ_DATA[14:8]}),
    .in3({multiplexer_9_out, MEM_READ_DATA[14:0]}), .in4({multiplexer_7_out, MEM_READ_DATA[22:16]}),
    .in8({multiplexer_8_out, MEM_READ_DATA[30:24]}), .in12({multiplexer_10_out, MEM_READ_DATA[30:16]}),
    .in15(MEM_READ_DATA), .out(MEM_Read), .sel(select_bits_for_reading));  // open: in0, in5, in6, in7, in9, in10, in11, in13, in14

  // Other names for the same wires on the sheet: OPCODE[6:0] = INSTRUCTION[6:0]; RD[4:0] = INSTRUCTION[11:7];
  //   FUNC3[2:0] = INSTRUCTION[14:12]; U_UJ_In[19:0] = INSTRUCTION[31:12]; RS1[4:0] = INSTRUCTION[19:15];
  //   RS2[4:0] = INSTRUCTION[24:20]; FUNC7[6:0] = INSTRUCTION[31:25]; Bottom_2[1:0] = Address[1:0];
  //   Result[31:0] = Address; Upper_30[29:0] = Address[31:2]

  // Notes on the sheet:
  //   Output to IMEM
  //   SPLITER
  //   IMEM (do **NOT** move this)
  //   Inputs from IMEM
  //   It is OK to move the PC, RegFile, ALU, MEM, Branch Comp, Imm Gen, and Control Logic to wherever is most convenient for you when constructing your CPU, and to delete this text
  //   Inputs/Outputs for testing. Do **NOT** move these.
  //   Outputs To DMEM
  //   DMEM (do **NOT** move this)
  //   Inputs From DMEM
endmodule
