// Logisim project imm-gen.circ as structural Verilog: 1 circuit, main circuit imm_gen
module imm_gen (
  input  [31:0] inst,
  input  [2:0] ImmSel,
  output [31:0] imm
);

  wire [31:12] I_TYPE_IMM_GEN, S_TYPE_IMM;
  wire [31:13] SB_TYPE_IMM;
  wire [31:21] UJ_TYPE_IMM;

  Multiplexer #(.enable("false"), .width(20)) multiplexer_1 (
    .in0({20{1'b0}}), .in1({20{1'b1}}), .out(I_TYPE_IMM_GEN), .sel(inst[31]));
  Multiplexer #(.enable("false"), .width(20)) multiplexer_2 (
    .in0({20{1'b0}}), .in1({20{1'b1}}), .out(S_TYPE_IMM), .sel(inst[31]));
  Multiplexer #(.enable("false"), .width(19)) multiplexer_3 (
    .in0({19{1'b0}}), .in1({19{1'b1}}), .out(SB_TYPE_IMM), .sel(inst[31]));
  Multiplexer #(.enable("false"), .select(3), .width(32)) multiplexer_4 (
    .in0({I_TYPE_IMM_GEN, inst[31:20]}), .in1({S_TYPE_IMM, inst[31:25], inst[11:7]}),
    .in2({SB_TYPE_IMM, inst[31], inst[7], inst[30:25], inst[11:8], 1'b0}), .in3({inst[31:12], {12{1'b0}}}),
    .in4({UJ_TYPE_IMM, inst[31], inst[19:12], inst[20], inst[30:21], 1'b0}), .in5({{27{1'b0}}, inst[19:15]}),
    .out(imm), .sel(ImmSel));  // open: in6, in7
  Multiplexer #(.enable("false"), .width(11)) multiplexer_5 (
    .in0({11{1'b0}}), .in1({11{1'b1}}), .out(UJ_TYPE_IMM), .sel(inst[31]));

  // Other names for the same wires on the sheet: OPCODE[6:0] = inst[6:0]; RD[4:0] = inst[11:7];
  //   S_TYPE_IMM[11:0] = {inst[31:25], inst[11:7]}; SB_TYPE_IMM[12:1] = {inst[31], inst[7], inst[30:25], inst[11:8]};
  //   I_TYPE_IMM_GEN[11:0] = inst[31:20]; imm_1_10[9:0] = inst[30:21]; RS2[4:0] = inst[24:20];
  //   U_TYPE_IMM[31:12] = inst[31:12]; U_UJ_In[19:0] = inst[31:12];
  //   UJ_TYPE_IMM[20:1] = {inst[31], inst[19:12], inst[20], inst[30:21]}; FUNC7[6:0] = inst[31:25]; imm_11 = inst[20];
  //   FUNC3[2:0] = inst[14:12]; imm_12_19[7:0] = inst[19:12]; CSRW_IMM[4:0] = inst[19:15]; RS1[4:0] = inst[19:15];
  //   imm_20 = inst[31]; sign_I = inst[31]

  // Notes on the sheet:
  //   INPUTS to your circuit
  //   SPLITER
  //   S Type Immediate Generator
  //   I Type Immediate Generator
  //   SB Type Immediate Generator
  //   DON'T CHANGE THE LOCATIONS OF THE INPUTS AND OUTPUTS!
  //   Constants
  //   U Type Immediate Generator
  //   UJ Type Immediate Generator
  //   OUTPUT from your circuit
endmodule
