// Logisim project regfile.circ as structural Verilog: 1 circuit, main circuit regfile
module regfile (
  input  [4:0] rs1,
  input  [4:0] rs2,
  input  [4:0] rd,
  input  [31:0] Write_Data,
  input  RegWEn,
  input  clk,
  output [31:0] ra,
  output [31:0] sp,
  output [31:0] t0,
  output [31:0] t1,
  output [31:0] t2,
  output [31:0] s0,
  output [31:0] s1,
  output [31:0] a0,
  output [31:0] Read_Data_1,
  output [31:0] Read_Data_2
);

  wire WE0, WE1, WE2, WE3, WE4, WE5, WE6, WE7, WE8, WE9, WE10, WE11, WE12, WE13, WE14, WE15, WE16, WE17,
       WE18, WE19, WE20, WE21, WE22, WE23, WE24, WE25, WE26, WE27, WE28, WE29, WE30, WE31;
  wire [31:0] D1, D2, D3, D4, D5, D6, D7, D8, D9, D10, D11, D12, D13, D14, D15, D16, D17, D18, D19, D20, D21,
       D22, D23, D24, D25, D26, D27, D28, D29, D30, D31, Q0, Q3, Q4, Q11, Q12, Q13, Q14, Q15, Q16, Q17, Q18,
       Q19, Q20, Q21, Q22, Q23, Q24, Q25, Q26, Q27, Q28, Q29, Q30, Q31;

  Register #(.width(32)) register_1 (.D({32{1'b0}}), .en(WE0), .clk(clk), .Q(Q0));  // open: clr
  Register #(.width(32)) register_2 (.D(D8), .en(WE8), .clk(clk), .Q(s0));  // open: clr
  Register #(.width(32)) register_3 (.D(D16), .en(WE16), .clk(clk), .Q(Q16));  // open: clr
  Register #(.width(32)) register_4 (.D(D24), .en(WE24), .clk(clk), .Q(Q24));  // open: clr
  Demultiplexer #(.enable("false"), .select(5), .width(32)) demultiplexer_1 (
    .out1(D1), .out2(D2), .out3(D3), .out4(D4), .out5(D5), .out6(D6), .out7(D7), .out8(D8), .out9(D9),
    .out10(D10), .out11(D11), .out12(D12), .out13(D13), .out14(D14), .out15(D15), .out16(D16), .out17(D17),
    .out18(D18), .out19(D19), .out20(D20), .out21(D21), .out22(D22), .out23(D23), .out24(D24), .out25(D25),
    .out26(D26), .out27(D27), .out28(D28), .out29(D29), .out30(D30), .out31(D31), .in(Write_Data), .sel(rd));  // open: out0
  Register #(.width(32)) register_5 (.D(D1), .en(WE1), .clk(clk), .Q(ra));  // open: clr
  Register #(.width(32)) register_6 (.D(D9), .en(WE9), .clk(clk), .Q(s1));  // open: clr
  Register #(.width(32)) register_7 (.D(D17), .en(WE17), .clk(clk), .Q(Q17));  // open: clr
  Register #(.width(32)) register_8 (.D(D25), .en(WE25), .clk(clk), .Q(Q25));  // open: clr
  Register #(.width(32)) register_9 (.D(D2), .en(WE2), .clk(clk), .Q(sp));  // open: clr
  Register #(.width(32)) register_10 (.D(D10), .en(WE10), .clk(clk), .Q(a0));  // open: clr
  Register #(.width(32)) register_11 (.D(D18), .en(WE18), .clk(clk), .Q(Q18));  // open: clr
  Register #(.width(32)) register_12 (.D(D26), .en(WE26), .clk(clk), .Q(Q26));  // open: clr
  Multiplexer #(.enable("false"), .select(5), .width(32)) multiplexer_1 (
    .in0(Q0), .in1(ra), .in2(sp), .in3(Q3), .in4(Q4), .in5(t0), .in6(t1), .in7(t2), .in8(s0), .in9(s1),
    .in10(a0), .in11(Q11), .in12(Q12), .in13(Q13), .in14(Q14), .in15(Q15), .in16(Q16), .in17(Q17),
    .in18(Q18), .in19(Q19), .in20(Q20), .in21(Q21), .in22(Q22), .in23(Q23), .in24(Q24), .in25(Q25),
    .in26(Q26), .in27(Q27), .in28(Q28), .in29(Q29), .in30(Q30), .in31(Q31), .out(Read_Data_1), .sel(rs1));
  Register #(.width(32)) register_13 (.D(D3), .en(WE3), .clk(clk), .Q(Q3));  // open: clr
  Register #(.width(32)) register_14 (.D(D11), .en(WE11), .clk(clk), .Q(Q11));  // open: clr
  Register #(.width(32)) register_15 (.D(D19), .en(WE19), .clk(clk), .Q(Q19));  // open: clr
  Register #(.width(32)) register_16 (.D(D27), .en(WE27), .clk(clk), .Q(Q27));  // open: clr
  Register #(.width(32)) register_17 (.D(D4), .en(WE4), .clk(clk), .Q(Q4));  // open: clr
  Register #(.width(32)) register_18 (.D(D12), .en(WE12), .clk(clk), .Q(Q12));  // open: clr
  Register #(.width(32)) register_19 (.D(D20), .en(WE20), .clk(clk), .Q(Q20));  // open: clr
  Register #(.width(32)) register_20 (.D(D28), .en(WE28), .clk(clk), .Q(Q28));  // open: clr
  Demultiplexer #(.enable("false"), .select(5)) demultiplexer_2 (
    .out1(WE1), .out2(WE2), .out3(WE3), .out4(WE4), .out5(WE5), .out6(WE6), .out7(WE7), .out8(WE8),
    .out9(WE9), .out10(WE10), .out11(WE11), .out12(WE12), .out13(WE13), .out14(WE14), .out15(WE15),
    .out16(WE16), .out17(WE17), .out18(WE18), .out19(WE19), .out20(WE20), .out21(WE21), .out22(WE22),
    .out23(WE23), .out24(WE24), .out25(WE25), .out26(WE26), .out27(WE27), .out28(WE28), .out29(WE29),
    .out30(WE30), .out31(WE31), .in(RegWEn), .sel(rd));  // open: out0
  Register #(.width(32)) register_21 (.D(D5), .en(WE5), .clk(clk), .Q(t0));  // open: clr
  Register #(.width(32)) register_22 (.D(D13), .en(WE13), .clk(clk), .Q(Q13));  // open: clr
  Register #(.width(32)) register_23 (.D(D21), .en(WE21), .clk(clk), .Q(Q21));  // open: clr
  Register #(.width(32)) register_24 (.D(D29), .en(WE29), .clk(clk), .Q(Q29));  // open: clr
  Register #(.width(32)) register_25 (.D(D6), .en(WE6), .clk(clk), .Q(t1));  // open: clr
  Register #(.width(32)) register_26 (.D(D14), .en(WE14), .clk(clk), .Q(Q14));  // open: clr
  Register #(.width(32)) register_27 (.D(D22), .en(WE22), .clk(clk), .Q(Q22));  // open: clr
  Register #(.width(32)) register_28 (.D(D30), .en(WE30), .clk(clk), .Q(Q30));  // open: clr
  Multiplexer #(.enable("false"), .select(5), .width(32)) multiplexer_2 (
    .in0(Q0), .in1(ra), .in2(sp), .in3(Q3), .in4(Q4), .in5(t0), .in6(t1), .in7(t2), .in8(s0), .in9(s1),
    .in10(a0), .in11(Q11), .in12(Q12), .in13(Q13), .in14(Q14), .in15(Q15), .in16(Q16), .in17(Q17),
    .in18(Q18), .in19(Q19), .in20(Q20), .in21(Q21), .in22(Q22), .in23(Q23), .in24(Q24), .in25(Q25),
    .in26(Q26), .in27(Q27), .in28(Q28), .in29(Q29), .in30(Q30), .in31(Q31), .out(Read_Data_2), .sel(rs2));
  Register #(.width(32)) register_29 (.D(D7), .en(WE7), .clk(clk), .Q(t2));  // open: clr
  Register #(.width(32)) register_30 (.D(D15), .en(WE15), .clk(clk), .Q(Q15));  // open: clr
  Register #(.width(32)) register_31 (.D(D23), .en(WE23), .clk(clk), .Q(Q23));  // open: clr
  Register #(.width(32)) register_32 (.D(D31), .en(WE31), .clk(clk), .Q(Q31));  // open: clr

  // Other names for the same wires on the sheet: Q1[31:0] = ra; Q2[31:0] = sp; Q5[31:0] = t0; Q6[31:0] = t1;
  //   Q7[31:0] = t2; Q8[31:0] = s0; Q9[31:0] = s1; Q10[31:0] = a0; read_data1[31:0] = Read_Data_1;
  //   read_data2[31:0] = Read_Data_2; read_reg1[4:0] = rs1; read_reg2[4:0] = rs2; write_en = RegWEn;
  //   write_reg[4:0] = rd

  // Notes on the sheet:
  //   INPUTS to your circuit
  //   DEBUG_OUTPUT
  //   RS1_MUX
  //   RD_DEMUX
  //   DON'T CHANGE THE LOCATIONS OF THE INPUTS AND OUTPUTS!
  //   These are DEBUG/TEST outputs from your circuit.
  //   RegFile
  //   RS1_MUX
  //   OUTPUTS from your circuit
  //   WE_MUX
endmodule
