// Logisim project cpu-far_jumps.circ as structural Verilog: 1 circuit, main circuit run_main
module run_main (
  output [31:0] ra,
  output [31:0] sp,
  output [31:0] t0,
  output [31:0] t1,
  output [31:0] t2,
  output [31:0] s0,
  output [31:0] s1,
  output [31:0] a0,
  output [31:0] Requested_Address,
  output [31:0] Requested_Instruction,
  output [15:0] Time_Step,
  output halt
);

  wire clk;

  Clock clock_1 (.out(clk));
  // Probe on Requested_Address
  // cpu_harness cpu_harness_1: pin names not known; wires that end beside it: Requested_Instruction, clk, Requested_Address, ra, sp, t0, t1, t2, s0, s1, a0
  ROM #(.addrWidth(14), .dataWidth(32)) rom_1 (.addr(Requested_Address[15:2]), .data(Requested_Instruction));
  // Probe on Requested_Instruction
  Counter #(.max('hffff), .width(16)) counter_1 (.clk(clk), .Q(Time_Step));  // open: clr, load, up, count, D, carry
  Comparator #(.width(16)) comparator_1 (.a(Time_Step), .b(16'h2a0), .eq(halt));  // open: gt, lt

  // Other names for the same wires on the sheet: INSTRUCTION[31:0] = Requested_Instruction;
  //   PROGRAM_COUNTER[31:0] = Requested_Address

  // Notes on the sheet:
  //   contents of rom_1 (hex, n*v repeats v):
  //   293 4000EF 128293 18000EF 100293 4000EF E4010EF 200293 FF1FF0EF 100293 100293 528333 5303B3 730E33
  //   1CE0EB3 1CE8F33 1DF0FB3 530433 5404B3 848933 12489B3 F9C00293 6428313 F8830393 7838E13 7838513
  //   2738E93 A7930F13 1EF0F93 F91E0413 F240493 FD550913 1940993 FFB90A13 348A93 217E8B13 FD2A0B93 2248C13
  //   22A8C93 1D098D13 17D0D93 156A0593 100293 528333 5303B3 730E33 1CE0EB3 1CE8F33 1DF0FB3 530433 5404B3
  //   848933 12489B3 F9C00293 6428313 F8830393 7838E13 7838513 2738E93 A7930F13 1EF0F93 F91E0413 F240493
  //   FD550913 1940993 FFB90A13 348A93 217E8B13 FD2A0B93 2248C13 22A8C93 1D098D13 17D0D93 156A0593 7B00293
  //   5EC00313 2533333 25333B3 263BE33 27E3EB3 3CEBF33 3DF3FB3 3EFB433 3F434B3 284B933 294B9B3 329BA33
  //   33A3AB3 34ABB33 35B3BB3 36BBC33 37C3CB3 38CBD33 39D38B3 3A8B833 31837B3 257B733 7B00293 5EC00313
  //   2533333 25333B3 263BE33 27E3EB3 3CEBF33 3DF3FB3 3EFB433 3F434B3 284B933 294B9B3 329BA33 33A3AB3
  //   34ABB33 35B3BB3 36BBC33 37C3CB3 38CBD33 39D38B3 3A8B833 31837B3 257B733 7B00293 5EC00313 2533333
  //   25333B3 263BE33 27E3EB3 3CEBF33 3DF3FB3 3EFB433 3F434B3 284B933 294B9B3 329BA33 33A3AB3 34ABB33
  //   35B3BB3 36BBC33 37C3CB3 38CBD33 39D38B3 3A8B833 31837B3 257B733 7B00293 5EC00313 2533333 25333B3
  //   263BE33 27E3EB3 3CEBF33 3DF3FB3 3EFB433 3F434B3 284B933 294B9B3 329BA33 33A3AB3 34ABB33 35B3BB3
  //   36BBC33 37C3CB3 38CBD33 39D38B3 3A8B833 31837B3 257B733 7B00293 5EC00313 2533333 25333B3 263BE33
  //   27E3EB3 3CEBF33 3DF3FB3 3EFB433 3F434B3 284B933 294B9B3 329BA33 33A3AB3 34ABB33 35B3BB3 36BBC33
  //   37C3CB3 38CBD33 39D38B3 3A8B833 31837B3 257B733 7B00293 5EC00313 2533333 25333B3 263BE33 27E3EB3
  //   3CEBF33 3DF3FB3 3EFB433 3F434B3 284B933 294B9B3 329BA33 33A3AB3 34ABB33 35B3BB3 36BBC33 37C3CB3
  //   38CBD33 39D38B3 3A8B833 31837B3 257B733 7B00293 5EC00313 2533333 25333B3 263BE33 27E3EB3 3CEBF33
  //   3DF3FB3 3EFB433 3F434B3 284B933 294B9B3 329BA33 33A3AB3 34ABB33 35B3BB3 36BBC33 37C3CB3 38CBD33
  //   39D38B3 3A8B833 31837B3 257B733 7B00293 5EC00313 2533333 25333B3 263BE33 27E3EB3 3CEBF33 3DF3FB3
  //   3EFB433 3F434B3 284B933 294B9B3 329BA33 33A3AB3 34ABB33 35B3BB3 36BBC33 37C3CB3 38CBD33 39D38B3
  //   3A8B833 31837B3 257B733 7B00293 5EC00313 2533333 25333B3 263BE33 27E3EB3 3CEBF33 3DF3FB3 3EFB433
  //   3F434B3 284B933 294B9B3 329BA33 33A3AB3 34ABB33 35B3BB3 36BBC33 37C3CB3 38CBD33 39D38B3 3A8B833
  //   31837B3 257B733 7B00293 5EC00313 2533333 25333B3 263BE33 27E3EB3 3CEBF33 3DF3FB3 3EFB433 3F434B3
  //   284B933 294B9B3 329BA33 33A3AB3 34ABB33 35B3BB3 36BBC33 37C3CB3 38CBD33 39D38B3 3A8B833 31837B3
  //   257B733 7B00293 5EC00313 2533333 25333B3 263BE33 27E3EB3 3CEBF33 3DF3FB3 3EFB433 3F434B3 284B933
  //   294B9B3 329BA33 33A3AB3 34ABB33 35B3BB3 36BBC33 37C3CB3 38CBD33 39D38B3 3A8B833 31837B3 257B733
  //   7B00293 5EC00313 2533333 25333B3 263BE33 27E3EB3 3CEBF33 3DF3FB3 3EFB433 3F434B3 284B933 294B9B3
  //   329BA33 33A3AB3 34ABB33 35B3BB3 36BBC33 37C3CB3 38CBD33 39D38B3 3A8B833 31837B3 257B733 7B00293
  //   5EC00313 2533333 25333B3 263BE33 27E3EB3 3CEBF33 3DF3FB3 3EFB433 3F434B3 284B933 294B9B3 329BA33
  //   33A3AB3 34ABB33 35B3BB3 36BBC33 37C3CB3 38CBD33 39D38B3 3A8B833 31837B3 257B733 7B00293 5EC00313
  //   2533333 25333B3 263BE33 27E3EB3 3CEBF33 3DF3FB3 3EFB433 3F434B3 284B933 294B9B3 329BA33 33A3AB3
  //   34ABB33 35B3BB3 36BBC33 37C3CB3 38CBD33 39D38B3 3A8B833 31837B3 257B733 7B00293 5EC00313 2533333
  //   25333B3 263BE33 27E3EB3 3CEBF33 3DF3FB3 3EFB433 3F434B3 284B933 294B9B3 329BA33 33A3AB3 34ABB33
  //   35B3BB3 36BBC33 37C3CB3 38CBD33 39D38B3 3A8B833 31837B3 257B733 7B00293 5EC00313 2533333 25333B3
  //   263BE33 27E3EB3 3CEBF33 3DF3FB3 3EFB433 3F434B3 284B933 294B9B3 329BA33 33A3AB3 34ABB33 35B3BB3
  //   36BBC33 37C3CB3 38CBD33 39D38B3 3A8B833 31837B3 257B733 7B00293 5EC00313 2533333 25333B3 263BE33
  //   27E3EB3 3CEBF33 3DF3FB3 3EFB433 3F434B3 284B933 294B9B3 329BA33 33A3AB3 34ABB33 35B3BB3 36BBC33
  //   37C3CB3 38CBD33 39D38B3 3A8B833 31837B3 257B733 7B00293 5EC00313 2533333 25333B3 263BE33 27E3EB3
  //   3CEBF33 3DF3FB3 3EFB433 3F434B3 284B933 294B9B3 329BA33 33A3AB3 34ABB33 35B3BB3 36BBC33 37C3CB3
  //   38CBD33 39D38B3 3A8B833 31837B3 257B733 7B00293 5EC00313 2533333 25333B3 263BE33 27E3EB3 3CEBF33
  //   3DF3FB3 3EFB433 3F434B3 28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
  //   Instruction Memory
  //   Halts Execution After Constant # of Clock Cycles
  //   Constant
endmodule
